// Logisim project Laba 4.circ as structural Verilog: 6 circuits, main circuit RS триггер с прямыми входами
module \RS_триггер_с_прямыми_входами  (
  input  R,
  input  S,
  output out_3,
  output out_4
);

  nor nor_1 (out_3, R, out_4);
  nor nor_2 (out_4, out_3, S);
endmodule

module \RS_триггер_с_инверсивными_входами  (
  input  R,
  input  S,
  output out_3,
  output out_4
);

  nand nand_1 (out_3, R, out_4);
  nand nand_2 (out_4, out_3, S);
endmodule

module \Синхронный_RS  (
  input  R,
  input  C,
  input  S,
  output out_4,
  output out_5
);

  wire nand_1_out, nand_2_out;

  nand nand_1 (nand_1_out, R, C);
  nand nand_2 (nand_2_out, C, S);
  nand nand_3 (out_4, nand_1_out, out_5);
  nand nand_4 (out_5, out_4, nand_2_out);
endmodule

module \S_триггер  (
  input  S,
  input  R,
  output out_3,
  output out_4
);

  wire nand_1_out, nand_2_out;

  nand nand_1 (nand_1_out, S, S);
  nand nand_2 (nand_2_out, nand_1_out, R);
  nand nand_3 (out_3, nand_1_out, out_4);
  nand nand_4 (out_4, out_3, nand_2_out);
endmodule

module \R_триггер  (
  input  S,
  input  R,
  output out_3,
  output out_4
);

  wire nand_1_out, nand_2_out;

  nand nand_1 (nand_1_out, S, nand_2_out);
  nand nand_2 (nand_2_out, R, R);
  nand nand_3 (out_3, nand_1_out, out_4);
  nand nand_4 (out_4, out_3, nand_2_out);
endmodule

module \E_триггер  (
  input  S,
  input  R,
  output out_3,
  output out_4
);

  wire nand_1_out, nand_2_out, nand_3_out, nand_4_out;

  nand nand_1 (nand_1_out, S, S);
  nand nand_2 (nand_2_out, R, R);
  nand nand_3 (nand_3_out, S, nand_2_out);
  nand nand_4 (nand_4_out, nand_1_out, R);
  nand nand_5 (out_3, nand_3_out, out_4);
  nand nand_6 (out_4, out_3, nand_4_out);
endmodule
