// Logisim project Laba 5.circ as structural Verilog: 2 circuits, main circuit D-триггер
module \D_триггер  (
  input  D,
  input  C,
  output Q,
  output Q_
);

  wire nand_1_out, nand_2_out;

  nand nand_1 (nand_1_out, D, D, C);
  nand nand_2 (nand_2_out, nand_1_out, C);
  nand nand_3 (Q, nand_1_out, Q_);
  nand nand_4 (Q_, Q, nand_2_out);
endmodule

module \Синхронный_Т_триггер  (
  input  \Т ,
  input  \С ,
  output out_3
);

  wire d_ff_1_qn, nand_1_out;

  nand nand_1 (nand_1_out, \Т , \С );
  D_Flip_Flop d_ff_1 (.clk(nand_1_out), .D(d_ff_1_qn), .Q(out_3), .Qn(d_ff_1_qn));  // open: preset, en, reset
endmodule
