// Logisim project Laba 6.circ as structural Verilog: 6 circuits, main circuit Схема сравнения
module \Схема_сравнения  (
  input  X1,
  input  X2,
  output Y
);

  wire and_1_out, and_2_out, not_1_out, not_2_out;

  not not_1 (not_1_out, X1);
  not not_2 (not_2_out, X2);
  and and_1 (and_1_out, not_1_out, X2);
  and and_2 (and_2_out, X1, not_2_out);
  or or_1 (Y, and_1_out, and_2_out);
endmodule

module \Полусумматор  (
  input  X1,
  input  X2,
  output out_3,
  output out_4
);

  \Схема_сравнения  \u_Схема_сравнения  (.X1(X1), .X2(X2), .Y(out_4));
  and and_1 (out_3, X1, X2);

  // Notes on the sheet:
  //   Старший разряд - перенос
  //   Младший разряд суммы
endmodule

// SM
module \Сумматор  (
  input  X1,
  input  X2,
  input  Pi,
  output P,
  output S
);

  wire \Полусумматор_2_out_3 , \Полусумматор_out_3 , \Полусумматор_out_4 ;

  \Полусумматор  \u_Полусумматор  (.X1(X1), .X2(X2), .out_3(\Полусумматор_out_3 ), .out_4(\Полусумматор_out_4 ));
  \Полусумматор  \u_Полусумматор_2  (.X1(\Полусумматор_out_4 ), .X2(Pi), .out_3(\Полусумматор_2_out_3 ), .out_4(S));
  or or_1 (P, \Полусумматор_out_3 , \Полусумматор_2_out_3 );

  // Notes on the sheet:
  //   Перенос
  //   Младший разряд суммы
endmodule

module \Схема_4_сумматоров  (
  input  X4,
  input  Y4,
  input  X3,
  input  Y3,
  input  X2,
  input  Y2,
  input  X1,
  input  Y1,
  input  P0,
  output S5,
  output S4,
  output S3,
  output S2,
  output S1
);

  wire \сумматор_1_p , \сумматор_2_p , \сумматор_3_p ;

  \Сумматор  \u_сумматор_1  (.X1(X1), .X2(Y1), .Pi(P0), .P(\сумматор_1_p ), .S(S1));
  \Сумматор  \u_сумматор_2  (.X1(X2), .X2(Y2), .Pi(\сумматор_1_p ), .P(\сумматор_2_p ), .S(S2));
  \Сумматор  \u_сумматор_3  (.X1(X3), .X2(Y3), .Pi(\сумматор_2_p ), .P(\сумматор_3_p ), .S(S3));
  \Сумматор  \u_сумматор_4  (.X1(X4), .X2(Y4), .Pi(\сумматор_3_p ), .P(S5), .S(S4));
endmodule

module \Полусумматор_из_теории  (
  input  A,
  input  B,
  output S,
  output P
);

  wire not_1_out, or_1_out;

  or or_1 (or_1_out, A, B);
  and and_1 (P, A, B);
  not not_1 (not_1_out, P);
  and and_2 (S, or_1_out, not_1_out);
endmodule

module \Сумматор_из_теории  (
  input  A,
  input  B,
  input  P0,
  output P,
  output S
);

  wire and_1_out, and_2_out, and_3_out, and_4_out, and_5_out, not_1_out, or_1_out;

  and and_1 (and_1_out, A, B);
  and and_2 (and_2_out, A, P0);
  and and_3 (and_3_out, B, P0);
  or or_1 (or_1_out, A, B, P0);
  and and_4 (and_4_out, A, B, P0);
  or or_2 (P, and_1_out, and_2_out, and_3_out);
  not not_1 (not_1_out, P);
  and and_5 (and_5_out, not_1_out, or_1_out);
  or or_3 (S, and_5_out, and_4_out);
endmodule
