// Logisim project Laba 7.circ as structural Verilog: 5 circuits, main circuit Простейший мультиплексор
module \Простейший_мультиплексор  (
  input  a,
  input  b,
  input  sel,
  output out
);

  wire and_1_out, and_2_out, not_1_out;

  not not_1 (not_1_out, sel);
  and and_1 (and_1_out, a, not_1_out);
  and and_2 (and_2_out, b, sel);
  or or_1 (out, and_1_out, and_2_out);
endmodule

// MUX
module \_4х_канальный_мультиплексор  (
  input  A0,
  input  A1,
  input  D0,
  input  D1,
  input  D2,
  input  D3,
  output Y
);

  wire and_1_out, and_2_out, and_3_out, and_4_out, not_1_out, not_2_out;

  not not_1 (not_1_out, A0);
  not not_2 (not_2_out, A1);
  and and_1 (and_1_out, not_1_out, D0, not_2_out);
  and and_2 (and_2_out, not_2_out, D1, A0);
  and and_3 (and_3_out, not_1_out, D2, A1);
  and and_4 (and_4_out, A1, D3, A0);
  or or_1 (Y, and_1_out, and_2_out, and_3_out, and_4_out);
endmodule

module \_16ти_канальный_мультиплексор  (
  input  D0,
  input  D1,
  input  D2,
  input  D3,
  input  D4,
  input  D5,
  input  D6,
  input  D7,
  input  D8,
  input  D9,
  input  D10,
  input  D11,
  input  D12,
  input  D13,
  input  D14,
  input  D15,
  input  A0,
  input  A1,
  input  A2,
  input  A3,
  output out_21
);

  wire \n4х_канальный_мультиплексор_1_y , \n4х_канальный_мультиплексор_2_y ,
       \n4х_канальный_мультиплексор_3_y , \n4х_канальный_мультиплексор_4_y ;

  \_4х_канальный_мультиплексор  \u_4х_канальный_мультиплексор_1  (
    .A0(A0), .A1(A1), .D0(D0), .D1(D1), .D2(D2), .D3(D3), .Y(\n4х_канальный_мультиплексор_1_y ));
  \_4х_канальный_мультиплексор  \u_4х_канальный_мультиплексор_2  (
    .A0(A0), .A1(A1), .D0(D4), .D1(D5), .D2(D6), .D3(D7), .Y(\n4х_канальный_мультиплексор_2_y ));
  \_4х_канальный_мультиплексор  \u_4х_канальный_мультиплексор_3  (
    .A0(A0), .A1(A1), .D0(D8), .D1(D9), .D2(D10), .D3(D11), .Y(\n4х_канальный_мультиплексор_3_y ));
  \_4х_канальный_мультиплексор  \u_4х_канальный_мультиплексор_4  (
    .A0(A0), .A1(A1), .D0(D12), .D1(D13), .D2(D14), .D3(D15), .Y(\n4х_канальный_мультиплексор_4_y ));
  \_4х_канальный_мультиплексор  \u_4х_канальный_мультиплексор_5  (
    .A0(A2), .A1(A3), .D0(\n4х_канальный_мультиплексор_1_y ), .D1(\n4х_канальный_мультиплексор_2_y ),
    .D2(\n4х_канальный_мультиплексор_3_y ), .D3(\n4х_канальный_мультиплексор_4_y ), .Y(out_21));
endmodule

module \Простейший_демультиплексор  (
  input  in,
  input  sel,
  output a,
  output b
);

  wire not_1_out;

  not not_1 (not_1_out, sel);
  and and_1 (a, in, not_1_out);
  and and_2 (b, in, sel);
endmodule

module \_16ти_канальный_мультиплексор__стандарт  (
  input  D0,
  input  D1,
  input  D2,
  input  D3,
  input  D4,
  input  D5,
  input  D6,
  input  D7,
  input  D8,
  input  D9,
  input  D10,
  input  D11,
  input  D12,
  input  D13,
  input  D14,
  input  D15,
  output out_17,
  output [3:0] out_18
);

  wire [3:0] undriven;

  Multiplexer #(.select(4)) multiplexer_1 (
    .in0(D0), .in1(D1), .in2(D2), .in3(D3), .in4(D4), .in5(D5), .in6(D6), .in7(D7), .in8(D8), .in9(D9),
    .in10(D10), .in11(D11), .in12(D12), .in13(D13), .in14(D14), .in15(D15), .out(out_17), .sel(undriven));  // open: en
endmodule
