// Logisim project Laba_3_Var_3.circ as structural Verilog: 2 circuits, main circuit schema1
module schema1 (
  input  a,
  input  b,
  input  c,
  input  d,
  output v1,
  output v2
);

  wire and_1_out, and_2_out, not_1_out, not_2_out;

  not not_1 (not_1_out, b);
  and and_1 (and_1_out, not_1_out, not_2_out);
  not not_2 (not_2_out, c);
  and and_2 (and_2_out, b, c);
  or or_1 (v2, and_1_out, d, and_2_out, a);

  assign v1 = 1'b0;
endmodule

module schema2 (
  input  a,
  input  b,
  input  c,
  input  d,
  output v1,
  output v2,
  output v3
);

  wire and_1_out, and_2_out, and_3_out, and_4_out, and_5_out, and_6_out, and_7_out, and_8_out, and_9_out,
       and_10_out, not_1_out, not_2_out, not_3_out, not_4_out, not_5_out, not_6_out, not_7_out, not_8_out,
       not_9_out, not_10_out, not_11_out, not_12_out, not_13_out, not_14_out, not_15_out, not_16_out,
       not_17_out, not_18_out, not_19_out, not_20_out;

  not not_1 (not_1_out, a);
  not not_2 (not_2_out, b);
  not not_3 (not_3_out, c);
  not not_4 (not_4_out, d);
  not not_5 (not_5_out, a);
  not not_6 (not_6_out, b);
  not not_7 (not_7_out, c);
  not not_8 (not_8_out, a);
  not not_9 (not_9_out, b);
  not not_10 (not_10_out, d);
  not not_11 (not_11_out, a);
  not not_12 (not_12_out, c);
  not not_13 (not_13_out, d);
  not not_14 (not_14_out, a);
  not not_15 (not_15_out, b);
  not not_16 (not_16_out, c);
  not not_17 (not_17_out, d);
  not not_18 (not_18_out, b);
  not not_19 (not_19_out, c);
  not not_20 (not_20_out, d);
  and and_1 (and_1_out, not_1_out, not_2_out, not_3_out, not_4_out);
  or or_1 (v1, and_1_out, and_2_out);
  and and_2 (and_2_out, a, b, c, d);
  and and_3 (and_3_out, not_5_out, not_6_out, not_7_out, d);
  and and_4 (and_4_out, not_8_out, not_9_out, c, not_10_out);
  and and_5 (and_5_out, not_11_out, b, not_12_out, not_13_out);
  and and_6 (and_6_out, not_14_out, b, c, d);
  and and_7 (and_7_out, a, not_15_out, not_16_out, not_17_out);
  and and_8 (and_8_out, a, not_18_out, c, d);
  and and_9 (and_9_out, a, b, not_19_out, d);
  and and_10 (and_10_out, a, b, c, not_20_out);
  or or_2 (v2, and_3_out, and_4_out, and_5_out, and_6_out, and_7_out, and_8_out, and_9_out, and_10_out);

  assign v3 = 1'b0;
endmodule
